// Logisim project som.circ as structural Verilog: 11 circuits, main circuit som
module som (
  output [4:0] out_1
);

  wire _0_out, _1_out, _2_out, _3_out, _4_out, _5_out, _6_out, _7_out, _8_out, _9_out, and_1_out, and_2_out,
       and_3_out, and_4_out, and_5_out, and_6_out, and_7_out, and_8_out, and_9_out, and_10_out, and_11_out,
       and_12_out, and_13_out, and_14_out, and_15_out, and_16_out, and_17_out, and_18_out, and_19_out,
       and_20_out, and_21_out, and_22_out, button_2_out, button_out, clock_1_out, d_ff_1_q, d_ff_2_q,
       d_ff_3_q, d_ff_4_q, d_ff_5_q, d_ff_6_q, d_ff_7_q, e_out, m_out, nand_1_out, not_1_out, not_2_out,
       not_3_out, not_4_out, not_5_out, on_out, or_6_out, teclado_1_out_12;
  wire [1:0] estado_1_out_3, or_1_out;
  wire [2:0] botao_1_out_3, botao_2_out_3, botao_3_out_3, botao_4_out_3, botao_5_out_3, botao_6_out_3,
       or_3_out, xor_1_out;
  wire [4:0] ant_1_out_4, maior31_1_out_3, n_1_1_out_2, n_1_2_out_2;
  wire [7:0] memtecl_1_out_2, teclado_1_out_13;

  Clock clock_1 (.out(clock_1_out));
  Button _7 (.out(_7_out));
  Button _4 (.out(_4_out));
  Button _1 (.out(_1_out));
  Button on (.out(on_out));
  Button m (.out(m_out));
  Button e (.out(e_out));
  Button button (.out(button_out));
  Button button_2 (.out(button_2_out));
  Button _8 (.out(_8_out));
  Button _9 (.out(_9_out));
  Button _6 (.out(_6_out));
  Button _5 (.out(_5_out));
  Button _2 (.out(_2_out));
  Button _3 (.out(_3_out));
  Button _0 (.out(_0_out));
  D_Flip_Flop d_ff_1 (
    .clk(clock_1_out), .D(teclado_1_out_12), .Q(d_ff_1_q), .preset(teclado_1_out_12));  // open: Qn, en, reset
  D_Flip_Flop d_ff_2 (.clk(clock_1_out), .D(on_out), .Q(d_ff_2_q), .preset(on_out));  // open: Qn, en, reset
  D_Flip_Flop d_ff_3 (.clk(clock_1_out), .D(m_out), .Q(d_ff_3_q), .preset(m_out));  // open: Qn, en, reset
  D_Flip_Flop d_ff_4 (.clk(clock_1_out), .D(e_out), .Q(d_ff_4_q), .preset(e_out));  // open: Qn, en, reset
  D_Flip_Flop d_ff_5 (.clk(clock_1_out), .D(button_out), .Q(d_ff_5_q), .preset(button_out));  // open: Qn, en, reset
  D_Flip_Flop d_ff_6 (.clk(clock_1_out), .D(button_2_out), .Q(d_ff_6_q), .preset(button_2_out));  // open: Qn, en, reset
  memtecl memtecl_1 (.in_1(teclado_1_out_13), .out_2(memtecl_1_out_2));
  teclado teclado_1 (
    .in_1(_7_out), .in_2(_8_out), .in_3(_9_out), .in_4(_4_out), .in_5(_5_out), .in_6(_6_out), .in_7(_1_out),
    .in_8(_2_out), .in_9(_3_out), .in_10(d_ff_7_q), .in_11(_0_out), .out_13(teclado_1_out_13),
    .out_12(teclado_1_out_12));
  botao botao_1 (.in_1(d_ff_1_q), .in_2(3'b101), .out_3(botao_1_out_3));
  botao botao_2 (.in_1(d_ff_2_q), .in_2(3'b110), .out_3(botao_2_out_3));
  botao botao_3 (.in_1(d_ff_3_q), .in_2(3'b001), .out_3(botao_3_out_3));
  ExactlyOne xor_1[2:0] (
    .out(xor_1_out), .in0(botao_1_out_3), .in1(botao_2_out_3), .in2(botao_3_out_3), .in3(botao_4_out_3),
    .in4(botao_5_out_3), .in5(botao_6_out_3));
  botao botao_4 (.in_1(d_ff_4_q), .in_2(3'b100), .out_3(botao_4_out_3));
  botao botao_5 (.in_1(d_ff_5_q), .in_2(3'b010), .out_3(botao_5_out_3));
  botao botao_6 (.in_1(d_ff_6_q), .in_2(3'b011), .out_3(botao_6_out_3));
  ant ant_1 (.in_1(out_1), .in_2(clock_1_out), .out_4(ant_1_out_4), .in_3(nand_1_out));
  maior31 maior31_1 (.in_1(ant_1_out_4), .in_2(memtecl_1_out_2), .out_3(maior31_1_out_3));
  not not_1 (not_1_out, xor_1_out[2]);
  not not_2 (not_2_out, xor_1_out[1]);
  n_1_2 n_1_1 (.in_1(ant_1_out_4), .out_2(n_1_1_out_2));
  n_1 n_1_2 (.in_1(ant_1_out_4), .out_2(n_1_2_out_2));
  Multiplexer #(.select(3), .width(5), .enable("false")) multiplexer_1 (
    .in0(5'b10001), .in1({5{1'b0}}), .in2(ant_1_out_4), .in3(n_1_1_out_2), .in4(n_1_2_out_2),
    .in5(maior31_1_out_3), .out(out_1), .sel(or_3_out));  // open: in6, in7
  not not_3 (not_3_out, xor_1_out[0]);
  not not_4 (not_4_out, estado_1_out_3[0]);
  not not_5 (not_5_out, estado_1_out_3[1]);
  nand nand_1 (nand_1_out, or_1_out[1], or_1_out[0]);
  estado estado_1 (.in_1(or_1_out), .in_2(clock_1_out), .out_3(estado_1_out_3));
  and and_1 (and_1_out, not_1_out, not_2_out, not_3_out, estado_1_out_3[0]);
  and and_2 (and_2_out, not_1_out, not_2_out, not_5_out, estado_1_out_3[0]);
  or or_1 (or_1_out[0], and_1_out, and_2_out, and_3_out, and_4_out);
  and and_3 (and_3_out, not_1_out, not_2_out, xor_1_out[0], not_4_out);
  and and_4 (and_4_out, not_2_out, xor_1_out[0], not_5_out, not_4_out);
  and and_5 (and_5_out, not_1_out, not_2_out, not_3_out, estado_1_out_3[1]);
  and and_6 (and_6_out, not_1_out, not_2_out, xor_1_out[0], not_4_out);
  or or_2 (or_1_out[1], and_5_out, and_6_out, and_7_out);
  and and_7 (and_7_out, not_2_out, xor_1_out[0], not_5_out, estado_1_out_3[0]);
  and and_8 (and_8_out, xor_1_out[1], xor_1_out[0]);
  and and_9 (and_9_out, not_1_out, xor_1_out[0], not_5_out);
  and and_10 (and_10_out, not_1_out, xor_1_out[0], not_5_out);
  or or_3 (or_3_out[0], and_8_out, and_9_out, and_10_out, and_11_out, and_12_out);
  and and_11 (and_11_out, xor_1_out[2], not_2_out, not_3_out);
  and and_12 (and_12_out, not_2_out, not_3_out, estado_1_out_3[1], estado_1_out_3[0]);
  and and_13 (and_13_out, xor_1_out[1], xor_1_out[0]);
  and and_14 (and_14_out, xor_1_out[2], xor_1_out[0]);
  or or_4 (or_3_out[1], and_13_out, and_14_out, and_15_out, and_16_out, and_17_out);
  and and_15 (and_15_out, xor_1_out[0], estado_1_out_3[1], estado_1_out_3[0]);
  and and_16 (and_16_out, not_1_out, not_2_out, not_3_out, not_5_out);
  and and_17 (and_17_out, not_1_out, not_2_out, not_3_out, not_4_out);
  and and_18 (and_18_out, not_1_out, xor_1_out[1], not_3_out);
  or or_5 (or_3_out[2], and_18_out, and_19_out);
  and and_19 (and_19_out, xor_1_out[2], not_2_out, not_3_out);
  and and_20 (and_20_out, xor_1_out[2], not_3_out);
  or or_6 (or_6_out, and_20_out, and_21_out, and_22_out);
  and and_21 (and_21_out, not_1_out, not_2_out, xor_1_out[0]);
  and and_22 (and_22_out, xor_1_out[2], estado_1_out_3[1], not_4_out);
  D_Flip_Flop d_ff_7 (.clk(clock_1_out), .D(or_6_out), .Q(d_ff_7_q));  // open: Qn, preset, en, reset
endmodule

module digito (
  input  in_1,
  input  [3:0] in_2,
  output [3:0] out_3
);

  wire [3:0] bit_extender_1_out;

  assign bit_extender_1_out = {{3{in_1}}, in_1};  // Bit_Extender bit_extender_1
  assign out_3 = bit_extender_1_out & in_2;  // AND_Gate and_1, 4 bits wide
endmodule

module teclado (
  input  in_1,
  input  in_2,
  input  in_3,
  input  in_4,
  input  in_5,
  input  in_6,
  input  in_7,
  input  in_8,
  input  in_9,
  input  in_10,
  input  in_11,
  output out_12,
  output [7:0] out_13
);

  wire or_1_out;
  wire [3:0] d_ff_4_q, digito_1_out_3, digito_2_out_3, digito_3_out_3, digito_4_out_3, digito_5_out_3,
       digito_6_out_3, digito_7_out_3, digito_8_out_3, digito_9_out_3, digito_10_out_3, or_3_out;
  wire [7:0] multiplier_1_out, register_1_q;

  or or_1 (or_1_out, in_10, out_12);
  D_Flip_Flop d_ff_1 (
    .D(or_3_out[3]), .Q(d_ff_4_q[3]), .preset(or_3_out[3]), .en(or_1_out), .reset(or_1_out));  // open: clk, Qn
  digito digito_1 (.in_1(in_1), .in_2(4'b0111), .out_3(digito_1_out_3));
  digito digito_2 (.in_1(in_4), .in_2(4'b0100), .out_3(digito_2_out_3));
  digito digito_3 (.in_1(in_7), .in_2(4'b0001), .out_3(digito_3_out_3));
  digito digito_4 (.in_1(in_11), .in_2(4'b0000), .out_3(digito_4_out_3));
  D_Flip_Flop d_ff_2 (
    .D(or_3_out[2]), .Q(d_ff_4_q[2]), .preset(or_3_out[2]), .en(or_1_out), .reset(or_1_out));  // open: clk, Qn
  or or_2 (out_12, in_11, in_7, in_4, in_1, in_8, in_5, in_2, in_9, in_6, in_3);
  digito digito_5 (.in_1(in_2), .in_2(4'b1000), .out_3(digito_5_out_3));
  digito digito_6 (.in_1(in_5), .in_2(4'b0101), .out_3(digito_6_out_3));
  digito digito_7 (.in_1(in_8), .in_2(4'b0010), .out_3(digito_7_out_3));
  D_Flip_Flop d_ff_3 (
    .D(or_3_out[1]), .Q(d_ff_4_q[1]), .preset(or_3_out[1]), .en(or_1_out), .reset(or_1_out));  // open: clk, Qn
  D_Flip_Flop d_ff_4 (
    .D(or_3_out[0]), .Q(d_ff_4_q[0]), .preset(or_3_out[0]), .en(or_1_out), .reset(or_1_out));  // open: clk, Qn
  assign or_3_out = digito_4_out_3 | digito_3_out_3 | digito_2_out_3 | digito_1_out_3 | digito_7_out_3 | digito_6_out_3 | digito_5_out_3 | digito_10_out_3 | digito_9_out_3 | digito_8_out_3;  // OR_Gate or_3, 4 bits wide
  digito digito_8 (.in_1(in_3), .in_2(4'b1001), .out_3(digito_8_out_3));
  digito digito_9 (.in_1(in_6), .in_2(4'b0110), .out_3(digito_9_out_3));
  digito digito_10 (.in_1(in_9), .in_2(4'b0011), .out_3(digito_10_out_3));
  Multiplier multiplier_1 (.a(8'ha), .b(register_1_q), .out(multiplier_1_out));  // open: cin, cout
  Register register_1 (.D({4'b0000, d_ff_4_q}), .en(or_1_out), .Q(register_1_q), .clk(or_1_out), .clr(in_10));
  Adder adder_1 (.a({4'b0000, d_ff_4_q}), .b(multiplier_1_out), .out(out_13));  // open: cin, cout
endmodule

module n_1 (
  input  [4:0] in_1,
  output [4:0] out_2
);

  wire and_1_out, nand_1_out;

  nand nand_1 (nand_1_out, in_1[0], in_1[1], in_1[2], in_1[3], in_1[4]);
  and and_1 (and_1_out, nand_1_out, 1'b1);
  Adder #(.width(5)) adder_1 (.a(in_1), .b({5{1'b0}}), .out(out_2), .cin(and_1_out));  // open: cout
endmodule

module n_1_2 (
  input  [4:0] in_1,
  output [4:0] out_2
);

  wire and_1_out, or_1_out;

  or or_1 (or_1_out, in_1[0], in_1[1], in_1[2], in_1[3], in_1[4]);
  and and_1 (and_1_out, or_1_out, 1'b1);
  Subtractor #(.width(5)) subtractor_1 (.a(in_1), .b({5{1'b0}}), .out(out_2), .bin(and_1_out));  // open: bout
endmodule

module ant (
  input  [4:0] in_1,
  input  in_2,
  input  in_3,
  output [4:0] out_4
);

  D_Flip_Flop d_ff_1 (.clk(in_2), .D(in_1[4]), .Q(out_4[4]), .en(in_3));  // open: Qn, preset, reset
  D_Flip_Flop d_ff_2 (.clk(in_2), .D(in_1[3]), .Q(out_4[3]), .en(in_3));  // open: Qn, preset, reset
  D_Flip_Flop d_ff_3 (.clk(in_2), .D(in_1[2]), .Q(out_4[2]), .en(in_3));  // open: Qn, preset, reset
  D_Flip_Flop d_ff_4 (.clk(in_2), .D(in_1[0]), .Q(out_4[0]), .en(in_3));  // open: Qn, preset, reset
  D_Flip_Flop d_ff_5 (.clk(in_2), .D(in_1[1]), .Q(out_4[1]), .en(in_3));  // open: Qn, preset, reset
endmodule

module saida (
  input  [2:0] in_1,
  input  in_2,
  output [2:0] out_3
);

  D_Flip_Flop d_ff_1 (.clk(in_2), .D(in_1[2]), .Q(out_3[2]));  // open: Qn, preset, en, reset
  D_Flip_Flop d_ff_2 (.clk(in_2), .D(in_1[1]), .Q(out_3[1]));  // open: Qn, preset, en, reset
  D_Flip_Flop d_ff_3 (.clk(in_2), .D(in_1[0]), .Q(out_3[0]));  // open: Qn, preset, en, reset
endmodule

module estado (
  input  [1:0] in_1,
  input  in_2,
  output [1:0] out_3
);

  D_Flip_Flop d_ff_1 (.clk(in_2), .D(in_1[1]), .Q(out_3[1]));  // open: Qn, preset, en, reset
  D_Flip_Flop d_ff_2 (.clk(in_2), .D(in_1[0]), .Q(out_3[0]));  // open: Qn, preset, en, reset
endmodule

module botao (
  input  in_1,
  input  [2:0] in_2,
  output [2:0] out_3
);

  wire [2:0] bit_extender_1_out;

  assign bit_extender_1_out = {{2{in_1}}, in_1};  // Bit_Extender bit_extender_1
  assign out_3 = bit_extender_1_out & in_2;  // AND_Gate and_1, 3 bits wide
endmodule

module memtecl (
  input  [7:0] in_1,
  output [7:0] out_2
);

  wire or_1_out;

  Register #(.trigger("high")) register_1 (.D(in_1), .en(or_1_out), .Q(out_2), .clk(or_1_out));  // open: clr
  or or_1 (or_1_out, in_1[7], in_1[6], in_1[5], in_1[4], in_1[3], in_1[2], in_1[1], in_1[0]);
endmodule

module maior31 (
  input  [4:0] in_1,
  input  [7:0] in_2,
  output [4:0] out_3
);

  wire comparator_1_eq, comparator_1_gt, comparator_1_lt, or_1_out;
  wire [4:0] and_1_out, and_2_out, bit_extender_1_out, bit_extender_2_out;

  Comparator comparator_1 (.a(in_2), .b(8'h1f), .gt(comparator_1_gt), .eq(comparator_1_eq), .lt(comparator_1_lt));
  or or_1 (or_1_out, comparator_1_eq, comparator_1_lt);
  assign bit_extender_1_out = {{4{or_1_out}}, or_1_out};  // Bit_Extender bit_extender_1
  assign bit_extender_2_out = {{4{comparator_1_gt}}, comparator_1_gt};  // Bit_Extender bit_extender_2
  assign and_1_out = in_1 & bit_extender_2_out;  // AND_Gate and_1, 5 bits wide
  assign and_2_out = bit_extender_1_out & in_2[4:0];  // AND_Gate and_2, 5 bits wide
  assign out_3 = and_1_out | and_2_out;  // OR_Gate or_2, 5 bits wide
endmodule
